// Logisim project Mult 2x1(8bits).circ as structural Verilog: 1 circuit, main circuit main
module main (
  input  \Endereço ,
  input  [7:0] _0,
  input  [7:0] _1,
  output [7:0] \Saída 
);

  wire and_1_out, and_2_out, and_3_out, and_4_out, and_5_out, and_6_out, and_7_out, and_8_out, and_9_out,
       and_10_out, and_11_out, and_12_out, and_13_out, and_14_out, and_15_out, and_16_out;

  and and_1 (and_1_out, ~\Endereço , _0[0]);  // AND_Gate
  and and_2 (and_2_out, \Endereço , _1[0]);
  and and_3 (and_3_out, ~\Endereço , _0[1]);  // AND_Gate
  and and_4 (and_4_out, \Endereço , _1[1]);
  and and_5 (and_5_out, ~\Endereço , _0[2]);  // AND_Gate
  and and_6 (and_6_out, \Endereço , _1[2]);
  and and_7 (and_7_out, ~\Endereço , _0[3]);  // AND_Gate
  and and_8 (and_8_out, \Endereço , _1[3]);
  and and_9 (and_9_out, ~\Endereço , _0[4]);  // AND_Gate
  and and_10 (and_10_out, \Endereço , _1[4]);
  and and_11 (and_11_out, ~\Endereço , _0[5]);  // AND_Gate
  and and_12 (and_12_out, \Endereço , _1[5]);
  and and_13 (and_13_out, ~\Endereço , _0[6]);  // AND_Gate
  and and_14 (and_14_out, \Endereço , _1[6]);
  and and_15 (and_15_out, ~\Endereço , _0[7]);  // AND_Gate
  and and_16 (and_16_out, \Endereço , _1[7]);
  or or_1 (\Saída [0], and_1_out, and_2_out);
  or or_2 (\Saída [1], and_3_out, and_4_out);
  or or_3 (\Saída [2], and_5_out, and_6_out);
  or or_4 (\Saída [3], and_7_out, and_8_out);
  or or_5 (\Saída [4], and_9_out, and_10_out);
  or or_6 (\Saída [5], and_11_out, and_12_out);
  or or_7 (\Saída [6], and_13_out, and_14_out);
  or or_8 (\Saída [7], and_15_out, and_16_out);
endmodule
