// Logisim project ProcessadorFINAL.circ as structural Verilog: 8 circuits, main circuit main
module main (
  input  Clock,
  input  Clear,
  input  [7:0] Dado,
  output [7:0] \Saída 
);

  D_Flip_Flop d_ff_1 (.clk(Clock), .D(Dado[7]), .Q(\Saída [7]), .reset(Clear));  // open: Qn, preset, en
  D_Flip_Flop d_ff_2 (.clk(Clock), .D(Dado[6]), .Q(\Saída [6]), .reset(Clear));  // open: Qn, preset, en
  D_Flip_Flop d_ff_3 (.clk(Clock), .D(Dado[5]), .Q(\Saída [5]), .reset(Clear));  // open: Qn, preset, en
  D_Flip_Flop d_ff_4 (.clk(Clock), .D(Dado[4]), .Q(\Saída [4]), .reset(Clear));  // open: Qn, preset, en
  D_Flip_Flop d_ff_5 (.clk(Clock), .D(Dado[3]), .Q(\Saída [3]), .reset(Clear));  // open: Qn, preset, en
  D_Flip_Flop d_ff_6 (.clk(Clock), .D(Dado[1]), .Q(\Saída [1]), .reset(Clear));  // open: Qn, preset, en
  D_Flip_Flop d_ff_7 (.clk(Clock), .D(Dado[2]), .Q(\Saída [2]), .reset(Clear));  // open: Qn, preset, en
  D_Flip_Flop d_ff_8 (.clk(Clock), .D(Dado[0]), .Q(\Saída [0]), .reset(Clear));  // open: Qn, preset, en
endmodule

module UC (
  input  Enable,
  input  [2:0] in_2,
  output RegWrite,
  output MemRead,
  output MemWrite,
  output MemToReg,
  output Branch,
  output Jump,
  output ULASrc,
  output [1:0] ULAOP
);

  wire demultiplexer_1_out2, demultiplexer_1_out3;

  Demultiplexer #(.select(3), .enable("false")) demultiplexer_1 (
    .out0(MemRead), .out1(MemWrite), .out2(demultiplexer_1_out2), .out3(demultiplexer_1_out3), .out4(Branch),
    .out5(Jump), .in(Enable), .sel(in_2));  // open: out6, out7
  or or_1 (ULASrc, MemRead, MemWrite);
  or or_2 (RegWrite, MemRead, demultiplexer_1_out2, demultiplexer_1_out3);
  Multiplexer #(.select(3), .width(2), .enable("false")) multiplexer_1 (
    .in0(2'b10), .in1(2'b10), .in2(2'b10), .in3(2'b11), .in4(2'b11), .out(ULAOP), .sel(in_2));  // open: in5, in6, in7

  assign MemToReg = MemRead;
endmodule

module Somador_4 (
  input  [7:0] in_1,
  output [7:0] out_2
);

  Adder adder_1 (.a(in_1), .b(8'h4), .out(out_2));  // open: cin, cout
endmodule

module ULA (
  input  [7:0] EntA,
  input  [7:0] EntB,
  input  [1:0] ULAOP,
  output [7:0] \Saída ,
  output Zero
);

  wire subtractor_1_bout;
  wire [7:0] adder_1_out, and_1_out, or_1_out, subtractor_1_out;

  assign and_1_out = EntA & EntB;  // AND_Gate and_1, 8 bits wide
  assign or_1_out = EntA | EntB;  // OR_Gate or_1, 8 bits wide
  Adder adder_1 (.a(EntA), .b(EntB), .out(adder_1_out));  // open: cin, cout
  Subtractor subtractor_1 (.a(EntA), .b(EntB), .out(subtractor_1_out), .bout(subtractor_1_bout));  // open: bin
  Multiplexer #(.select(2), .width(8)) multiplexer_1 (
    .in0(and_1_out), .in1(or_1_out), .in2(adder_1_out), .in3(subtractor_1_out), .out(\Saída ), .sel(ULAOP));  // open: en
  and and_2 (Zero, ~\Saída [0], ~\Saída [1], ~\Saída [2], ~\Saída [3], ~\Saída [4], ~\Saída [5], ~\Saída [6], ~\Saída [7], ~subtractor_1_bout);  // AND_Gate
endmodule

module BR (
  input  Clear,
  input  [7:0] Valor_a_atribuir,
  input  Clock,
  input  Enable,
  input  [1:0] \Endereço_1 ,
  input  [1:0] Write_Register,
  input  [1:0] \Endereço_2 ,
  output [7:0] R1_XX,
  output [7:0] R2_XX
);

  wire demultiplexer_1_out0, demultiplexer_1_out1, demultiplexer_1_out2, demultiplexer_1_out3;
  wire [7:0] \main_1_saída , \main_2_saída , \main_3_saída , \main_4_saída ;

  Demultiplexer #(.select(2)) demultiplexer_1 (
    .out0(demultiplexer_1_out0), .out1(demultiplexer_1_out1), .out2(demultiplexer_1_out2),
    .out3(demultiplexer_1_out3), .in(Clock), .sel(Write_Register), .en(Enable));
  main main_1 (.Clock(demultiplexer_1_out0), .Clear(Clear), .Dado(Valor_a_atribuir), .\Saída (\main_1_saída ));
  main main_2 (.Clock(demultiplexer_1_out1), .Clear(Clear), .Dado(Valor_a_atribuir), .\Saída (\main_2_saída ));
  main main_3 (.Clock(demultiplexer_1_out2), .Clear(Clear), .Dado(Valor_a_atribuir), .\Saída (\main_3_saída ));
  main main_4 (.Clock(demultiplexer_1_out3), .Clear(Clear), .Dado(Valor_a_atribuir), .\Saída (\main_4_saída ));
  Multiplexer #(.select(2), .width(8), .enable("false")) multiplexer_1 (
    .in0(\main_1_saída ), .in1(\main_2_saída ), .in2(\main_3_saída ), .in3(\main_4_saída ), .out(R1_XX),
    .sel(\Endereço_1 ));
  Multiplexer #(.select(2), .width(8), .enable("false")) multiplexer_2 (
    .in0(\main_1_saída ), .in1(\main_2_saída ), .in2(\main_3_saída ), .in3(\main_4_saída ), .out(R2_XX),
    .sel(\Endereço_2 ));
endmodule

module Mux_2x1 (
  input  \Endereço ,
  input  [7:0] _0,
  input  [7:0] _1,
  output [7:0] \Saída 
);

  wire and_1_out, and_2_out, and_3_out, and_4_out, and_5_out, and_6_out, and_7_out, and_8_out, and_9_out,
       and_10_out, and_11_out, and_12_out, and_13_out, and_14_out, and_15_out, and_16_out;

  and and_1 (and_1_out, ~\Endereço , _0[0]);  // AND_Gate
  and and_2 (and_2_out, \Endereço , _1[0]);
  and and_3 (and_3_out, ~\Endereço , _0[1]);  // AND_Gate
  and and_4 (and_4_out, \Endereço , _1[1]);
  and and_5 (and_5_out, ~\Endereço , _0[2]);  // AND_Gate
  and and_6 (and_6_out, \Endereço , _1[2]);
  and and_7 (and_7_out, ~\Endereço , _0[3]);  // AND_Gate
  and and_8 (and_8_out, \Endereço , _1[3]);
  and and_9 (and_9_out, ~\Endereço , _0[4]);  // AND_Gate
  and and_10 (and_10_out, \Endereço , _1[4]);
  and and_11 (and_11_out, ~\Endereço , _0[5]);  // AND_Gate
  and and_12 (and_12_out, \Endereço , _1[5]);
  and and_13 (and_13_out, ~\Endereço , _0[6]);  // AND_Gate
  and and_14 (and_14_out, \Endereço , _1[6]);
  and and_15 (and_15_out, ~\Endereço , _0[7]);  // AND_Gate
  and and_16 (and_16_out, \Endereço , _1[7]);
  or or_1 (\Saída [0], and_1_out, and_2_out);
  or or_2 (\Saída [1], and_3_out, and_4_out);
  or or_3 (\Saída [2], and_5_out, and_6_out);
  or or_4 (\Saída [3], and_7_out, and_8_out);
  or or_5 (\Saída [4], and_9_out, and_10_out);
  or or_6 (\Saída [5], and_11_out, and_12_out);
  or or_7 (\Saída [6], and_13_out, and_14_out);
  or or_8 (\Saída [7], and_15_out, and_16_out);
endmodule

// R2V
module Processador (
  input  Clear,
  output [1:0] out_2,
  output [7:0] out_3,
  output [7:0] OPCODE,
  output [2:0] OP,
  output [1:0] RA,
  output [1:0] RB,
  output [7:0] Valor_RA,
  output [7:0] Valor_RB,
  output [7:0] Entrada_ULA_1,
  output [7:0] Entrada_ULA_2,
  output [7:0] Saida_da_ULA,
  output [7:0] Entrada_de_Dado_Memoria,
  output [7:0] Para_Reg,
  output [1:0] Salvar_Reg,
  output [7:0] DM,
  output [7:0] I
);

  wire and_1_out, Clock, uc_1_branch, uc_1_jump, uc_1_memread, uc_1_memtoreg, uc_1_memwrite, uc_1_regwrite,
       uc_1_ulasrc, ula_1_zero;
  wire [7:0] adder_1_out, multiplexer_2_out, ram_1_data, register_1_q, shifter_1_out, shifter_2_out,
       somador_4_1_out_2;

  Clock u_Clock (.out(Clock));
  Register register_1 (.D(DM), .Q(register_1_q), .clk(Clock), .clr(Clear));  // open: en
  ROM rom_1 (.addr(register_1_q), .data({OP, OPCODE[4:1], I[0]}));  // open: sel
  Somador_4 somador_4_1 (.in_1(register_1_q), .out_2(somador_4_1_out_2));
  Shifter shifter_1 (
    .in({1'b0, somador_4_1_out_2[7:6], OPCODE[3], OPCODE[4], OPCODE[1], OPCODE[2], I[0]}), .\dist (3'b010),
    .out(shifter_1_out));
  BR br_1 (
    .Valor_a_atribuir(Para_Reg), .Clock(Clock), .R1_XX(Entrada_ULA_1), .R2_XX(Entrada_de_Dado_Memoria),
    .Clear(Clear), .\Endereço_1 ({OPCODE[3], OPCODE[4]}), .\Endereço_2 ({OPCODE[1], OPCODE[2]}),
    .Enable(uc_1_regwrite), .Write_Register({OPCODE[1], OPCODE[2]}));
  UC uc_1 (
    .Enable(1'b1), .RegWrite(uc_1_regwrite), .MemRead(uc_1_memread), .MemWrite(uc_1_memwrite),
    .MemToReg(uc_1_memtoreg), .Branch(uc_1_branch), .Jump(uc_1_jump), .ULAOP(out_2), .in_2(OP),
    .ULASrc(uc_1_ulasrc));
  Multiplexer #(.width(8), .enable("false")) multiplexer_1 (
    .in0(Entrada_de_Dado_Memoria), .in1({{7{1'b0}}, I[0]}), .out(Entrada_ULA_2), .sel(uc_1_ulasrc));
  Multiplexer #(.width(8), .enable("false")) multiplexer_2 (
    .in0(somador_4_1_out_2), .in1(shifter_1_out), .out(multiplexer_2_out), .sel(uc_1_jump));
  ULA ula_1 (.\Saída (out_3), .Zero(ula_1_zero), .EntA(Entrada_ULA_1), .EntB(Entrada_ULA_2), .ULAOP(out_2));
  Shifter shifter_2 (.in({{7{1'b0}}, I[0]}), .\dist (3'b010), .out(shifter_2_out));
  Adder adder_1 (.a(multiplexer_2_out), .b(shifter_2_out), .out(adder_1_out));  // open: cin, cout
  and and_1 (and_1_out, uc_1_branch, ula_1_zero);
  Multiplexer #(.width(8), .enable("false")) multiplexer_3 (
    .in0(multiplexer_2_out), .in1(adder_1_out), .out(DM), .sel(and_1_out));
  RAM #(.bus("separate")) ram_1 (
    .addr(out_3), .din(Entrada_de_Dado_Memoria), .data(ram_1_data), .str(uc_1_memwrite), .clk(Clock),
    .ld(uc_1_memread));  // open: sel, clr
  Multiplexer #(.width(8), .enable("false")) multiplexer_4 (
    .in0(out_3), .in1(ram_1_data), .out(Para_Reg), .sel(uc_1_memtoreg));

  assign I[7:1] = {7{1'b0}};
  assign {OPCODE[7:5], OPCODE[0]} = {OP, I[0]};
  assign RA = {OPCODE[3], OPCODE[4]};
  assign RB = {OPCODE[1], OPCODE[2]};
  assign Saida_da_ULA = out_3;
  assign Salvar_Reg = {OPCODE[1], OPCODE[2]};
  assign Valor_RA = Entrada_ULA_1;
  assign Valor_RB = Entrada_de_Dado_Memoria;

  // Other names for the same wires on the sheet: Imediato[0] = I[0]; DeslocMemoria[7:0] = DM;
  //   R1[1:0] = {OPCODE[3], OPCODE[4]}; MEMENTRADA[7:0] = Entrada_de_Dado_Memoria; R2V[7:0] = Entrada_de_Dado_Memoria;
  //   R2[1:0] = {OPCODE[1], OPCODE[2]}; RS[1:0] = {OPCODE[1], OPCODE[2]}; ToRegister[7:0] = Para_Reg;
  //   R1V[7:0] = Entrada_ULA_1; ULA1[7:0] = Entrada_ULA_1; ULA2[7:0] = Entrada_ULA_2; ULAS[7:0] = out_3

  // Notes on the sheet:
  //   contents of rom_1 (hex, n*v repeats v):
  //   11 0 0 0 29 0 0 0 43 0 0 0 54 0 0 0 12
endmodule

module Processador2 (
  input  Enable,
  input  in_2
);

  wire and_1_out, Clock, uc_1_branch, uc_1_jump, uc_1_memread, uc_1_memtoreg, uc_1_memwrite, uc_1_regwrite,
       uc_1_ulasrc, ula_1_zero;
  wire [1:0] uc_1_ulaop;
  wire [7:0] adder_1_out, br_1_r1_xx, br_1_r2_xx, multiplexer_1_out, multiplexer_2_out, multiplexer_3_out,
       multiplexer_4_out, ram_1_data, register_1_q, rom_1_data, shifter_1_out, shifter_2_out,
       somador_4_1_out_2, \ula_1_saída ;

  Clock clock_1 (.out(Clock));
  Register register_1 (.D(multiplexer_3_out), .Q(register_1_q), .clk(Clock), .clr(in_2));  // open: en
  ROM rom_1 (.addr(register_1_q), .data(rom_1_data));  // open: sel
  Somador_4 somador_4_1 (.in_1(register_1_q), .out_2(somador_4_1_out_2));
  Shifter shifter_1 (
    .in({1'b0, somador_4_1_out_2[7:6], rom_1_data[3], rom_1_data[4], rom_1_data[1], rom_1_data[2], rom_1_data[0]}),
    .\dist (3'b010), .out(shifter_1_out));
  BR br_1 (
    .Valor_a_atribuir(multiplexer_4_out), .Clock(Clock), .R1_XX(br_1_r1_xx), .R2_XX(br_1_r2_xx),
    .Clear(in_2), .\Endereço_1 ({rom_1_data[3], rom_1_data[4]}),
    .\Endereço_2 ({rom_1_data[1], rom_1_data[2]}), .Enable(uc_1_regwrite),
    .Write_Register({rom_1_data[1], rom_1_data[2]}));
  UC uc_1 (
    .Enable(Enable), .RegWrite(uc_1_regwrite), .MemRead(uc_1_memread), .MemWrite(uc_1_memwrite),
    .MemToReg(uc_1_memtoreg), .Branch(uc_1_branch), .Jump(uc_1_jump), .ULAOP(uc_1_ulaop),
    .in_2(rom_1_data[7:5]), .ULASrc(uc_1_ulasrc));
  Multiplexer #(.width(8), .enable("false")) multiplexer_1 (
    .in0(br_1_r2_xx), .in1({{7{1'b0}}, rom_1_data[0]}), .out(multiplexer_1_out), .sel(uc_1_ulasrc));
  Multiplexer #(.width(8), .enable("false")) multiplexer_2 (
    .in0(somador_4_1_out_2), .in1(shifter_1_out), .out(multiplexer_2_out), .sel(uc_1_jump));
  ULA ula_1 (
    .\Saída (\ula_1_saída ), .Zero(ula_1_zero), .EntA(br_1_r1_xx), .EntB(multiplexer_1_out),
    .ULAOP(uc_1_ulaop));
  Shifter shifter_2 (.in({{7{1'b0}}, rom_1_data[0]}), .\dist (3'b010), .out(shifter_2_out));
  Adder adder_1 (.a(multiplexer_2_out), .b(shifter_2_out), .out(adder_1_out));  // open: cin, cout
  and and_1 (and_1_out, uc_1_branch, ula_1_zero);
  Multiplexer #(.width(8), .enable("false")) multiplexer_3 (
    .in0(multiplexer_2_out), .in1(adder_1_out), .out(multiplexer_3_out), .sel(and_1_out));
  RAM #(.bus("separate")) ram_1 (
    .addr(\ula_1_saída ), .din(br_1_r2_xx), .data(ram_1_data), .str(uc_1_memwrite), .clk(Clock),
    .ld(uc_1_memread));  // open: sel, clr
  Multiplexer #(.width(8), .enable("false")) multiplexer_4 (
    .in0(\ula_1_saída ), .in1(ram_1_data), .out(multiplexer_4_out), .sel(uc_1_memtoreg));

  // Other names for the same wires on the sheet: Clear = in_2

  // Notes on the sheet:
  //   contents of rom_1 (hex, n*v repeats v):
  //   4*0 29
endmodule
