// Logisim project Memoria ROM.circ as structural Verilog: 2 circuits, main circuit main
module main (
  input  [1:0] \Endereço_para_Acesso ,
  input  Ativar,
  output out_3,
  output out_4,
  output out_5,
  output out_6,
  output out_7,
  output out_8,
  output out_9,
  output out_10
);

  ROM #(.addrWidth(2)) rom_1 (
    .addr(\Endereço_para_Acesso ), .data({out_3, out_4, out_5, out_6, out_7, out_8, out_9, out_10}),
    .sel(Ativar));

  // Notes on the sheet:
  //   contents of rom_1 (hex, n*v repeats v):
  //   1 2 3 5
endmodule

module Circuito_ROm (
  input  [1:0] \Endereço ,
  input  Ativar,
  output [7:0] Saida
);

  wire [7:0] register_1_q, register_2_q, register_3_q, register_4_q;

  Register register_1 (.Q(register_1_q));  // open: D, en, clk, clr
  Register register_2 (.Q(register_2_q));  // open: D, en, clk, clr
  Multiplexer #(.select(2), .width(8)) multiplexer_1 (
    .in0(register_1_q), .in1(register_2_q), .in2(register_3_q), .in3(register_4_q), .out(Saida),
    .sel(\Endereço ), .en(Ativar));
  Register register_3 (.Q(register_3_q));  // open: D, en, clk, clr
  Register register_4 (.Q(register_4_q));  // open: D, en, clk, clr

  // Notes on the sheet:
  //   Registradores
endmodule
