// Logisim project Somador.circ as structural Verilog: 3 circuits, main circuit main
module main (
  input  cin,
  input  A,
  input  B,
  output s,
  output Cout
);

  wire and_1_out, and_2_out, xor_1_out;

  xor xor_1 (xor_1_out, A, B);
  and and_1 (and_1_out, A, B);
  xor xor_2 (s, cin, xor_1_out);
  and and_2 (and_2_out, cin, xor_1_out);
  or or_1 (Cout, and_2_out, and_1_out);
endmodule

module Somador__1 (
  input  _7,
  input  _6,
  input  _5,
  input  _4,
  input  _3,
  input  _2,
  input  _1,
  input  _0,
  input  in_9,
  output [7:0] out_10,
  output Overflow
);

  wire adder_1_cout, adder_2_cout, adder_3_cout, adder_4_cout, adder_5_cout, adder_6_cout, adder_7_cout;

  Adder #(.width(1)) adder_1 (.a(_0), .b(1'b1), .out(out_10[0]), .cin(in_9), .cout(adder_1_cout));
  Adder #(.width(1)) adder_2 (.a(_1), .b(1'b0), .out(out_10[1]), .cin(adder_1_cout), .cout(adder_2_cout));
  Adder #(.width(1)) adder_3 (.a(_2), .b(1'b0), .out(out_10[2]), .cin(adder_2_cout), .cout(adder_3_cout));
  Adder #(.width(1)) adder_4 (.a(_3), .b(1'b0), .out(out_10[3]), .cin(adder_3_cout), .cout(adder_4_cout));
  Adder #(.width(1)) adder_5 (.a(_4), .b(1'b0), .out(out_10[4]), .cin(adder_4_cout), .cout(adder_5_cout));
  Adder #(.width(1)) adder_6 (.a(_5), .b(1'b0), .out(out_10[5]), .cin(adder_5_cout), .cout(adder_6_cout));
  Adder #(.width(1)) adder_7 (.a(_6), .b(1'b0), .out(out_10[6]), .cin(adder_6_cout), .cout(adder_7_cout));
  Adder #(.width(1)) adder_8 (.a(_7), .b(1'b0), .out(out_10[7]), .cin(adder_7_cout), .cout(Overflow));
endmodule

module Somador_8bits (
  input  A7,
  input  A6,
  input  A5,
  input  A4,
  input  A3,
  input  A2,
  input  A1,
  input  A0,
  input  B7,
  input  B6,
  input  B5,
  input  B4,
  input  B3,
  input  B2,
  input  B1,
  input  B,
  output [7:0] out_17,
  output Overflow
);

  wire adder_1_cout, adder_2_cout, adder_3_cout, adder_4_cout, adder_5_cout, adder_6_cout, adder_7_cout;

  Adder #(.width(1)) adder_1 (.a(A0), .b(B), .out(out_17[0]), .cin(1'b0), .cout(adder_1_cout));
  Adder #(.width(1)) adder_2 (.a(A1), .b(B1), .out(out_17[1]), .cin(adder_1_cout), .cout(adder_2_cout));
  Adder #(.width(1)) adder_3 (.a(A2), .b(B2), .out(out_17[2]), .cin(adder_2_cout), .cout(adder_3_cout));
  Adder #(.width(1)) adder_4 (.a(A3), .b(B3), .out(out_17[3]), .cin(adder_3_cout), .cout(adder_4_cout));
  Adder #(.width(1)) adder_5 (.a(A4), .b(B4), .out(out_17[4]), .cin(adder_4_cout), .cout(adder_5_cout));
  Adder #(.width(1)) adder_6 (.a(A5), .b(B5), .out(out_17[5]), .cin(adder_5_cout), .cout(adder_6_cout));
  Adder #(.width(1)) adder_7 (.a(A6), .b(B6), .out(out_17[6]), .cin(adder_6_cout), .cout(adder_7_cout));
  Adder #(.width(1)) adder_8 (.a(A7), .b(B7), .out(out_17[7]), .cin(adder_7_cout), .cout(Overflow));
endmodule
