// Logisim project ULA.circ as structural Verilog: 1 circuit, main circuit main
module main (
  input  [7:0] EntA,
  input  [7:0] EntB,
  input  [1:0] ULAOP,
  output [7:0] \Saída ,
  output Zero
);

  wire subtractor_1_bout;
  wire [7:0] adder_1_out, and_1_out, or_1_out, subtractor_1_out;

  assign and_1_out = EntA & EntB;  // AND_Gate and_1, 8 bits wide
  assign or_1_out = EntA | EntB;  // OR_Gate or_1, 8 bits wide
  Adder adder_1 (.a(EntA), .b(EntB), .out(adder_1_out));  // open: cin, cout
  Subtractor subtractor_1 (.a(EntA), .b(EntB), .out(subtractor_1_out), .bout(subtractor_1_bout));  // open: bin
  Multiplexer #(.select(2), .width(8)) multiplexer_1 (
    .in0(and_1_out), .in1(or_1_out), .in2(adder_1_out), .in3(subtractor_1_out), .out(\Saída ), .sel(ULAOP));  // open: en
  and and_2 (Zero, ~\Saída [0], ~\Saída [1], ~\Saída [2], ~\Saída [3], ~\Saída [4], ~\Saída [5], ~\Saída [6], ~\Saída [7], ~subtractor_1_bout);  // AND_Gate
endmodule
