// Logisim project Unidade de controle.circ as structural Verilog: 1 circuit, main circuit main
module main (
  input  Enable,
  input  [2:0] in_2,
  output RegWrite,
  output MemRead,
  output MemWrite,
  output MemToReg,
  output Branch,
  output Jump,
  output ULASrc,
  output [1:0] ULAOP
);

  wire demultiplexer_1_out2, demultiplexer_1_out3;

  Demultiplexer #(.select(3), .enable("false")) demultiplexer_1 (
    .out0(MemRead), .out1(MemWrite), .out2(demultiplexer_1_out2), .out3(demultiplexer_1_out3), .out4(Branch),
    .out5(Jump), .in(Enable), .sel(in_2));  // open: out6, out7
  or or_1 (ULASrc, MemRead, MemWrite);
  or or_2 (RegWrite, MemRead, demultiplexer_1_out2, demultiplexer_1_out3);
  Multiplexer #(.select(3), .width(2), .enable("false")) multiplexer_1 (
    .in0(2'b10), .in1(2'b10), .in2(2'b10), .in3(2'b11), .in4(2'b11), .out(ULAOP), .sel(in_2));  // open: in5, in6, in7

  assign MemToReg = MemRead;
endmodule
